# Fritzing sketch mainBoard (saved by Fritzing 0.9.3b)
circuit board: 20cm x 15cm

parts:
  Teensy_3_1 = Teensy 3.1  # not connected
  Raspberry_Pi_1 = Raspberry Pi 3 [part_number=RPI-3-V1.2]  # not connected
  IC1 = MCP2515 [package=THT]
  XTAL1 = Crystal [frequency="16 Mhz" package=SMD]
  R1 = Resistor [tolerance=±5% resistance=10k package=THT]
  J1 = double row female pin header, 12 pins [form="♀ (female)"]
  J2 = female pin header, 2 pins [form="♀ (female)"]
  J3 = female pin header, 2 pins [form="♀ (female)"]
  J4 = female pin header, 2 pins [form="♀ (female)"]
  J5 = double row female pin header, 40 pins [form="♀ (female)"]
  J6 = female pin header, 14 pins [form="♀ (female)"]
  J7 = female pin header, 14 pins [form="♀ (female)"]
  LED1 = LED - 3mm [color="Red (633nm)" package="3 mm [THT]"]
  LED2 = LED - 3mm [color="Red (633nm)" package="3 mm [THT]"]
  LED3 = LED - 3mm [color="Red (633nm)" package="3 mm [THT]"]
  J9 = female pin header, 3 pins [form="♀ (female)"]  # not connected
  J8 = female pin header, 3 pins [form="♀ (female)"]  # not connected
  J12 = double row female pin header, 12 pins [form="♀ (female)"]
  Fuse1 = Fuse with Handler [part_number=Htc-15m]
  Fuse2 = Fuse with Handler [part_number=Htc-15m]
  Fuse3 = Fuse with Handler [part_number=Htc-15m]
  Fuse4 = Fuse with Handler [part_number=Htc-15m]
  Fuse5 = Fuse with Handler [part_number=Htc-15m]
  IC2 = IC, DIP package, 8 pins [chip_label=IC]
  J13 = female pin header, 2 pins [form="♀ (female)"]
  J14 = female pin header, 3 pins [form="♀ (female)"]
  R2 = Resistor [tolerance=±5% resistance=120 package=THT]
  R3 = Resistor [tolerance=±5% resistance=22k package=THT]
  C1 = Ceramic Capacitor [capacitance=22pF package="100 mil [THT, multilayer]"]
  C2 = Ceramic Capacitor [capacitance=22pF package="100 mil [THT, multilayer]"]
  R4 = Resistor [tolerance=±5% resistance=4.7k package=THT]
  R5 = Resistor [tolerance=±5% resistance=4.7k package=THT]
  R6 = Resistor [tolerance=±5% resistance=4.7k package=THT]
  J11 = double row female pin header, 8 pins [form="♀ (female)"]

nets:
  N1: IC1.TXCAN, IC2.pin1
  N2: IC1.RXCAN, R1.Pin_1, R3.Pin_1
  N3: IC1.OSC2, XTAL1.pin_0, C1.0
  N4: IC1.OSC1, XTAL1.pin_1, C2.0
  N5: IC1.Vss, IC2.pin2, IC2.pin8, R3.Pin_0, C1.1, C2.1, J11.pin7
  N6: IC1.INT, J5.pin31, R6.Pin_1
  N7: IC1.CS, J5.pin32, R5.Pin_1
  N8: IC1.RESET, R4.Pin_0
  N9: IC1.Vdd, J5.pin12, R4.Pin_1, R5.Pin_0, R6.Pin_0
  N10: R1.Pin_0, IC2.pin4
  N11: J1.pin1, J6.pin11
  N12: J1.pin2, J6.pin10
  N13: J1.pin3, J12.pin10
  N14: J1.pin4, J2.pin1, J3.pin1, J4.pin1, J5.pin16, J7.pin14, J13.pin2, J14.pin3
  N15: J1.pin5, J6.pin9
  N16: J1.pin6, J6.pin8
  N17: J2.pin2, LED1.cathode
  N18: J3.pin2, LED3.cathode
  N19: J4.pin2, LED2.cathode
  N20: J5.pin21, J12.pin11, IC2.pin3
  N21: J6.pin14, J12.pin9, J11.pin2
  N22: J7.pin9, J11.pin4
  N23: J7.pin10, J14.pin1
  N24: LED1.anode, Fuse1.Connector1
  N25: LED2.anode, Fuse2.Connector1
  N26: LED3.anode, Fuse3.Connector1, Fuse4.Connector1, Fuse5.Connector1
  N27: J12.pin1, J11.pin8
  N28: J12.pin2, Fuse5.Connector2
  N29: J12.pin3, Fuse4.Connector2
  N30: J12.pin4, Fuse3.Connector2
  N31: J12.pin5, Fuse2.Connector2
  N32: J12.pin6, Fuse1.Connector2
  N33: J12.pin7, J13.pin1
  N34: J12.pin8, J14.pin2
  N35: J12.pin12, J11.pin1
  N36: IC2.pin6, R2.Pin_1, J11.pin6
  N37: IC2.pin7, R2.Pin_0, J11.pin5

notes:
  12V
  7.4V
  5V
  Temp
  Water
  Servo
  Motor
  Ch4 Ch3 GND 5V Ch1 Ch2
  Tx Rx  -  -  D- D+
  Pompe

custom parts:
  MCP2515: MCP2515 CAN Controller with SPI Interface
