# Fritzing sketch matBoard (saved by Fritzing 0.9.3b)
circuit board: 8.73478cm x 6.03955cm

parts:
  J1 = double row female pin header, 12 pins [form="♀ (female)"]
  J2 = female pin header, 5 pins [form="♀ (female)"]
  J4 = female pin header, 4 pins [form="♀ (female)"]
  J3 = double row female pin header, 12 pins [form="♀ (female)"]

nets:
  N1: J1.pin1, J3.pin11
  N2: J1.pin3, J3.pin10
  N3: J1.pin5, J3.pin9
  N4: J1.pin6, J3.pin8
  N5: J1.pin7, J3.pin7
  N6: J1.pin8, J4.pin1
  N7: J1.pin9, J2.pin4, J4.pin4
  N8: J1.pin11, J2.pin5
  N9: J1.pin12, J3.pin12
  N10: J2.pin2, J3.pin2
  N11: J2.pin3, J3.pin1
  N12: J4.pin2, J3.pin6
  N13: J4.pin3, J3.pin5

notes:
  GNSS
  XBee
  RC
  5V
  5V D+ D- GND
  RST Rx Tx GND 5V
  1
  2
  3
  4
  Ch4 Ch3 GND 5V Ch1 Ch2
  Tx Rx  -  -  D- D+
